// Digital circuit CPU_RISCV.dig as structural Verilog
module CPU_RISCV (
  input  [31:0] A,
  input  [31:0] B,
  input  [3:0] ALUControl,
  input  clk,
  input  reset,
  input  RegWrite,
  input  [4:0] rs1,
  input  [4:0] rs2,
  input  [4:0] rd,
  input  [31:0] WriteData,
  output [31:0] Result,
  output Zero,
  output [31:0] ReadData1,
  output [31:0] ReadData2
);

  RegisterFile_32 #(.applicationType("IVERILOG"), .CodeFile("/Users/kellysoares/Documents/Faculdade/arqComp/RICV_entrega/RegisterFile_32.v")) u_RegisterFile_32 (
    .clk(clk), .reset(reset), .RegWrite(RegWrite), .rs1(rs1), .rs2(rs2), .rd(rd), .WriteData(WriteData),
    .ReadData1(ReadData1), .ReadData2(ReadData2));
  ALU_32 #(.applicationType("IVERILOG"), .CodeFile("/Users/kellysoares/Documents/Faculdade/arqComp/RICV_entrega/ALU_32.v")) u_ALU_32 (
    .A(ReadData1), .B(ReadData2), .ALUControl(ALUControl), .Result(Result), .Zero(Zero));
endmodule
